# Fritzing sketch light-my-led (saved by Fritzing 0.9.2b)
breadboards: 1

parts:
  Onderdeel1 = Arduino Uno (Rev3)
  R1 = Resistor [tolerance=±5% resistance=330 package=THT]
  R2 = Resistor [tolerance=±5% resistance=330 package=THT]
  LED1 = LED - 5mm [color="Red (633nm)" package="5 mm [THT]"]
  LED2 = LED - 5mm [color="Yellow (595nm)" package="5 mm [THT]"]

nets:
  N1: Onderdeel1.D12/MISO, R1.Pin_0
  N2: Onderdeel1.D13/SCK, R2.Pin_0
  N3: Onderdeel1.GND, LED1.cathode, LED2.cathode
  N4: R1.Pin_1, LED2.anode
  N5: R2.Pin_1, LED1.anode
